# Fritzing sketch waterrocket_promini (saved by Fritzing 0.9.3b)
circuit board: 8.46667cm x 5.64444cm
breadboards: 1

parts:
  R1 = Resistor [tolerance=±5% resistance=220 package=THT]
  LED1 = LED - 5mm [color="Red (633nm)" package="5 mm [THT]"]
  Command_button = Pushbutton [package="[THT]"]
  "Breakwire" = Toggle Switch [package=THT]
  10DOF = 10DOF L3GD20 LSM303D BMP180
  SD_card_module1 = SD Card Module
  Onderdeel3 = Arduino Pro Mini v13
  C1 = Electrolytic Capacitor [capacitance=1µF package="100 mil [THT, electrolytic]"]
  J1 = Basic Servo
  U1 = LIPO-110mAh [package=lipo-110]
  Reset_button = Pushbutton [package="[THT]"]

nets:
  N1: R1.Pin_0, Onderdeel3.D9_PWM
  N2: R1.Pin_1, LED1.anode
  GND: LED1.cathode, Command_button.Pin_3, Command_button.Pin_4, "Breakwire".COM, 10DOF.GND, SD_card_module1.GND, Onderdeel3.GND, C1.-, Reset_button.Pin_1, Reset_button.Pin_2
  N3: Command_button.Pin_1, Command_button.Pin_2, Onderdeel3.D7
  N4: "Breakwire".L2, Onderdeel3.D8
  3V3: 10DOF.3V3, SD_card_module1.3.3V, Onderdeel3.VCC, C1.+
  N5: 10DOF.SCL, Onderdeel3.A5
  N6: 10DOF.SDA, Onderdeel3.A4
  N7: SD_card_module1.MISO#4, Onderdeel3.D12/MISO
  N8: SD_card_module1.SCK, Onderdeel3.D13/SCK
  N9: SD_card_module1.MISO#6, Onderdeel3.D11_PWM/MOSI
  N10: SD_card_module1.CS, Onderdeel3.D10_PWM/SS
  N11: Onderdeel3.DTR, U1.-
  N12: Onderdeel3.RAW, U1.+
  N13: Onderdeel3.A0, J1.pulse
  N14: Onderdeel3.RESET, Reset_button.Pin_3, Reset_button.Pin_4

custom parts:
  10DOF L3GD20 LSM303D BMP180: Dimensions: 22 mm × 17 mm Operating voltage: 2.5 V to 5.5 V Supply current: 8mA Output format (I2C/SPI): Gyro: one 16-bit reading per axis Accelerometer: one 16-bit reading per axis Magnetometer: one 16-bit reading per axis Barometer: 24-bit pressure reading (I2C only) Gyro: ±245, ±500, or ±2000°/s Accelerometer: ±2, ±4, ±6, ±8, or ±16 g Magnetometer: ±2, ±4, ±8, or ±12 gauss Barometer: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
  SD Card Module: SD Card Module Slot Socket Reader For Arduino ARM MCU
